# Fritzing sketch wiring (saved by Fritzing 1.0.4)
circuit board: 3.08417cm x 4.17732cm
breadboards: 1

parts:
  R4 = Resistor [tolerance=±5% power=0.25W resistance=1k package=THT]
  Q2 = NPN-Transistor [mpn=2N3904 package="TO92 [THT]"]
  R2 = Resistor [tolerance=±5% power=0.25W resistance=100 package=THT]
  Q1 = PNP-Transistor [mpn=2N3906 package="TO92 [THT]"]
  R1 = Resistor [tolerance=±5% power=0.25W resistance=47k package=THT]
  R3 = Resistor [tolerance=±5% power=0.25W resistance=4.7k package=THT]
  J1 = male pin header, 3 pins [form="♂ (male)"]
  J2 = male pin header, 2 pins [form="♂ (male)"]
  J3 = male pin header, 2 pins [form="♂ (male)"]

nets:
  N1: R4.Pin_0, J2.pin2
  N2: R4.Pin_1, Q2.B
  GND: Q2.E, J1.pin1, J3.pin2
  N3: Q2.C, R2.Pin_1
  N4: R2.Pin_0, Q1.B, R1.Pin_1
  3.3V: Q1.E, R1.Pin_0, J3.pin1
  N5: Q1.C, R3.Pin_0, J1.pin2
  N6: R3.Pin_1, J1.pin3, J2.pin1
